// Logisim project PC2.circ as structural Verilog: 9 circuits, main circuit main
module main (
);

  wire CLK, cu_1_alusrc, cu_1_memtoreg, Reset;
  wire [1:0] cu_1_aluop;
  wire [4:0] instruction_decoder_2_rd, instruction_decoder_2_rs, instruction_decoder_2_rt,
       instruction_decoder_2_shamt;
  wire [5:0] driver0, driver00, driver0a, driver0b, driver0c, driver0d, driver0e, driver0f, driver01,
       driver1, driver02, driver2, driver03, driver3, driver04, driver05, driver06, driver07, driver08,
       driver09, instruction_decoder_1_funct, instruction_decoder_1_opcode, instruction_decoder_2_funct,
       instruction_decoder_2_opcode;
  wire [6:0] display_driver_1_col0, display_driver_1_col1, display_driver_1_col2, display_driver_1_col3,
       display_driver_1_col4, display_driver_2_col0, display_driver_2_col1, display_driver_2_col2,
       display_driver_2_col3, display_driver_2_col4, display_driver_3_col0, display_driver_3_col1,
       display_driver_3_col2, display_driver_3_col3, display_driver_3_col4, display_driver_4_col0,
       display_driver_4_col1, display_driver_4_col2, display_driver_4_col3, display_driver_4_col4,
       display_driver_5_col0, display_driver_5_col1, display_driver_5_col2, display_driver_5_col3,
       display_driver_5_col4, display_driver_6_col0, display_driver_6_col1, display_driver_6_col2,
       display_driver_6_col3, display_driver_6_col4, display_driver_7_col0, display_driver_7_col1,
       display_driver_7_col2, display_driver_7_col3, display_driver_7_col4, display_driver_8_col0,
       display_driver_8_col1, display_driver_8_col2, display_driver_8_col3, display_driver_8_col4,
       display_driver_9_col0, display_driver_9_col1, display_driver_9_col2, display_driver_9_col3,
       display_driver_9_col4, display_driver_10_col0, display_driver_10_col1, display_driver_10_col2,
       display_driver_10_col3, display_driver_10_col4, display_driver_11_col0, display_driver_11_col1,
       display_driver_11_col2, display_driver_11_col3, display_driver_11_col4, display_driver_12_col0,
       display_driver_12_col1, display_driver_12_col2, display_driver_12_col3, display_driver_12_col4,
       display_driver_13_col0, display_driver_13_col1, display_driver_13_col2, display_driver_13_col3,
       display_driver_13_col4, display_driver_14_col0, display_driver_14_col1, display_driver_14_col2,
       display_driver_14_col3, display_driver_14_col4, display_driver_15_col0, display_driver_15_col1,
       display_driver_15_col2, display_driver_15_col3, display_driver_15_col4, display_driver_16_col0,
       display_driver_16_col1, display_driver_16_col2, display_driver_16_col3, display_driver_16_col4;
  wire [15:0] instruction_decoder_2_immediate;
  wire [23:0] PC;
  wire [25:0] instruction_decoder_2_address;
  wire [31:0] adder_1_out, Curr_Inst, register_1_q;

  Clock clock_1 (.out(CLK));
  Button button_1 (.out(Reset));
  // Probe on PC
  Register #(.width(32)) register_1 (.D(adder_1_out), .en(1'b1), .Q(register_1_q), .clk(CLK), .clr(Reset));
  // Probe on Curr_Inst
  Adder #(.width(32)) adder_1 (.a(32'h1), .b(register_1_q), .out(adder_1_out));  // open: cin, cout
  Bit_Extender #(.in_width(32), .out_width(24)) bit_extender_1 (.in(register_1_q), .out(PC));
  Instruction_Decoder instruction_decoder_1 (
    .Inst(Curr_Inst), .Opcode(instruction_decoder_1_opcode), .funct(instruction_decoder_1_funct));  // open: rs, rt, rd, shamt, Immediate, address
  RAM #(.addrWidth(24), .dataWidth(32)) ram_1 (
    .addr(PC), .data(Curr_Inst), .sel(1'b1), .clk(CLK), .ld(1'b1), .clr(1'b0));
  Debug_Circuit debug_circuit_1 (
    .Funct(instruction_decoder_1_funct), .Opcode(instruction_decoder_1_opcode), .inst3(driver03),
    .inst2(driver02), .inst1(driver01), .inst0(driver00), .out_8(driver04), .out_9(driver05),
    .out_10(driver06), .out_11(driver07), .out_12(driver08), .out_13(driver09), .out_14(driver0a),
    .out_15(driver0b), .out_16(driver0c), .out_17(driver0d), .out_18(driver0e), .out_19(driver0f));  // open: Inst
  Instruction_Decoder instruction_decoder_2 (
    .Inst(Curr_Inst), .Opcode(instruction_decoder_2_opcode), .rs(instruction_decoder_2_rs),
    .rt(instruction_decoder_2_rt), .rd(instruction_decoder_2_rd), .shamt(instruction_decoder_2_shamt),
    .funct(instruction_decoder_2_funct), .Immediate(instruction_decoder_2_immediate),
    .address(instruction_decoder_2_address));
  DotMatrix dotmatrix_1 (
    .col0(display_driver_1_col0), .col1(display_driver_1_col1), .col2(display_driver_1_col2),
    .col3(display_driver_1_col3), .col4(display_driver_1_col4));
  DotMatrix dotmatrix_2 (
    .col0(display_driver_2_col0), .col1(display_driver_2_col1), .col2(display_driver_2_col2),
    .col3(display_driver_2_col3), .col4(display_driver_2_col4));
  Display_Driver display_driver_1 (
    .col0(display_driver_1_col0), .col1(display_driver_1_col1), .col2(display_driver_1_col2),
    .col3(display_driver_1_col3), .col4(display_driver_1_col4), .in_1(driver0));
  DotMatrix dotmatrix_3 (
    .col0(display_driver_3_col0), .col1(display_driver_3_col1), .col2(display_driver_3_col2),
    .col3(display_driver_3_col3), .col4(display_driver_3_col4));
  Display_Driver display_driver_2 (
    .col0(display_driver_2_col0), .col1(display_driver_2_col1), .col2(display_driver_2_col2),
    .col3(display_driver_2_col3), .col4(display_driver_2_col4), .in_1(driver1));
  Display_Driver display_driver_3 (
    .col0(display_driver_3_col0), .col1(display_driver_3_col1), .col2(display_driver_3_col2),
    .col3(display_driver_3_col3), .col4(display_driver_3_col4), .in_1(driver2));
  CU cu_1 (
    .Opcode(instruction_decoder_2_opcode), .ALUSrc(cu_1_alusrc), .MemToReg(cu_1_memtoreg), .ALUOp(cu_1_aluop));  // open: Jump, RegDst, RegWrite, MemRead, MemWrite, Branch
  DotMatrix dotmatrix_4 (
    .col0(display_driver_4_col0), .col1(display_driver_4_col1), .col2(display_driver_4_col2),
    .col3(display_driver_4_col3), .col4(display_driver_4_col4));
  Display_Driver display_driver_4 (
    .col0(display_driver_4_col0), .col1(display_driver_4_col1), .col2(display_driver_4_col2),
    .col3(display_driver_4_col3), .col4(display_driver_4_col4), .in_1(driver3));
  DotMatrix dotmatrix_5 (
    .col0(display_driver_5_col0), .col1(display_driver_5_col1), .col2(display_driver_5_col2),
    .col3(display_driver_5_col3), .col4(display_driver_5_col4));
  RAM #(.addrWidth(24), .dataWidth(32)) ram_2 ();  // open: addr, data, sel, clk, ld, clr
  DotMatrix dotmatrix_6 (
    .col0(display_driver_6_col0), .col1(display_driver_6_col1), .col2(display_driver_6_col2),
    .col3(display_driver_6_col3), .col4(display_driver_6_col4));
  Display_Driver display_driver_5 (
    .col0(display_driver_5_col0), .col1(display_driver_5_col1), .col2(display_driver_5_col2),
    .col3(display_driver_5_col3), .col4(display_driver_5_col4), .in_1(driver0));
  Display_Driver display_driver_6 (
    .col0(display_driver_6_col0), .col1(display_driver_6_col1), .col2(display_driver_6_col2),
    .col3(display_driver_6_col3), .col4(display_driver_6_col4), .in_1(driver1));
  DotMatrix dotmatrix_7 (
    .col0(display_driver_7_col0), .col1(display_driver_7_col1), .col2(display_driver_7_col2),
    .col3(display_driver_7_col3), .col4(display_driver_7_col4));
  DotMatrix dotmatrix_8 (
    .col0(display_driver_8_col0), .col1(display_driver_8_col1), .col2(display_driver_8_col2),
    .col3(display_driver_8_col3), .col4(display_driver_8_col4));
  Display_Driver display_driver_7 (
    .col0(display_driver_7_col0), .col1(display_driver_7_col1), .col2(display_driver_7_col2),
    .col3(display_driver_7_col3), .col4(display_driver_7_col4), .in_1(driver2));
  Display_Driver display_driver_8 (
    .col0(display_driver_8_col0), .col1(display_driver_8_col1), .col2(display_driver_8_col2),
    .col3(display_driver_8_col3), .col4(display_driver_8_col4), .in_1(driver3));
  DotMatrix dotmatrix_9 (
    .col0(display_driver_11_col0), .col1(display_driver_11_col1), .col2(display_driver_11_col2),
    .col3(display_driver_11_col3), .col4(display_driver_11_col4));
  DotMatrix dotmatrix_10 (
    .col0(display_driver_9_col0), .col1(display_driver_9_col1), .col2(display_driver_9_col2),
    .col3(display_driver_9_col3), .col4(display_driver_9_col4));
  Display_Driver display_driver_9 (
    .col0(display_driver_9_col0), .col1(display_driver_9_col1), .col2(display_driver_9_col2),
    .col3(display_driver_9_col3), .col4(display_driver_9_col4), .in_1(driver0));
  ALU_Control alu_control_1 (.ALUOp(cu_1_aluop), .Funct(instruction_decoder_2_funct));  // open: Operation
  DotMatrix dotmatrix_11 (
    .col0(display_driver_10_col0), .col1(display_driver_10_col1), .col2(display_driver_10_col2),
    .col3(display_driver_10_col3), .col4(display_driver_10_col4));
  Display_Driver display_driver_10 (
    .col0(display_driver_10_col0), .col1(display_driver_10_col1), .col2(display_driver_10_col2),
    .col3(display_driver_10_col3), .col4(display_driver_10_col4), .in_1(driver2));
  Display_Driver display_driver_11 (
    .col0(display_driver_11_col0), .col1(display_driver_11_col1), .col2(display_driver_11_col2),
    .col3(display_driver_11_col3), .col4(display_driver_11_col4), .in_1(driver1));
  DotMatrix dotmatrix_12 (
    .col0(display_driver_12_col0), .col1(display_driver_12_col1), .col2(display_driver_12_col2),
    .col3(display_driver_12_col3), .col4(display_driver_12_col4));
  DotMatrix dotmatrix_13 (
    .col0(display_driver_14_col0), .col1(display_driver_14_col1), .col2(display_driver_14_col2),
    .col3(display_driver_14_col3), .col4(display_driver_14_col4));
  Display_Driver display_driver_12 (
    .col0(display_driver_12_col0), .col1(display_driver_12_col1), .col2(display_driver_12_col2),
    .col3(display_driver_12_col3), .col4(display_driver_12_col4), .in_1(driver3));
  DotMatrix dotmatrix_14 (
    .col0(display_driver_13_col0), .col1(display_driver_13_col1), .col2(display_driver_13_col2),
    .col3(display_driver_13_col3), .col4(display_driver_13_col4));
  Display_Driver display_driver_13 (
    .col0(display_driver_13_col0), .col1(display_driver_13_col1), .col2(display_driver_13_col2),
    .col3(display_driver_13_col3), .col4(display_driver_13_col4));  // open: in_1
  Display_Driver display_driver_14 (
    .col0(display_driver_14_col0), .col1(display_driver_14_col1), .col2(display_driver_14_col2),
    .col3(display_driver_14_col3), .col4(display_driver_14_col4));  // open: in_1
  DotMatrix dotmatrix_15 (
    .col0(display_driver_16_col0), .col1(display_driver_16_col1), .col2(display_driver_16_col2),
    .col3(display_driver_16_col3), .col4(display_driver_16_col4));
  DotMatrix dotmatrix_16 (
    .col0(display_driver_15_col0), .col1(display_driver_15_col1), .col2(display_driver_15_col2),
    .col3(display_driver_15_col3), .col4(display_driver_15_col4));
  Display_Driver display_driver_15 (
    .col0(display_driver_15_col0), .col1(display_driver_15_col1), .col2(display_driver_15_col2),
    .col3(display_driver_15_col3), .col4(display_driver_15_col4));  // open: in_1
  Display_Driver display_driver_16 (
    .col0(display_driver_16_col0), .col1(display_driver_16_col1), .col2(display_driver_16_col2),
    .col3(display_driver_16_col3), .col4(display_driver_16_col4));  // open: in_1
endmodule

module Instruction_Decoder (
  input  [31:0] Inst,
  output [5:0] Opcode,
  output [4:0] rs,
  output [4:0] rt,
  output [4:0] rd,
  output [4:0] shamt,
  output [5:0] funct,
  output [15:0] Immediate,
  output [25:0] address
);


  assign address = Inst[25:0];
  assign funct = Inst[5:0];
  assign Immediate = Inst[15:0];
  assign Opcode = Inst[31:26];
  assign rd = Inst[15:11];
  assign rs = Inst[25:21];
  assign rt = Inst[20:16];
  assign shamt = Inst[10:6];
endmodule

module CU (
  input  [5:0] Opcode,
  output Jump,
  output RegDst,
  output ALUSrc,
  output MemToReg,
  output RegWrite,
  output MemRead,
  output MemWrite,
  output Branch,
  output [1:0] ALUOp
);

  wire comparator_1_eq, comparator_2_eq, comparator_3_eq, comparator_4_eq, comparator_5_eq, comparator_6_eq;

  Comparator #(.width(6)) comparator_1 (.a(Opcode), .b({6{1'b0}}), .eq(comparator_1_eq));  // open: gt, lt
  Comparator #(.width(6)) comparator_2 (.a(Opcode), .b(6'b001000), .eq(comparator_2_eq));  // open: gt, lt
  Comparator #(.width(6)) comparator_3 (.a(Opcode), .b(6'b100011), .eq(comparator_3_eq));  // open: gt, lt
  Comparator #(.width(6)) comparator_4 (.a(Opcode), .b(6'b101011), .eq(comparator_4_eq));  // open: gt, lt
  Comparator #(.width(6)) comparator_5 (.a(Opcode), .b(6'b000100), .eq(comparator_5_eq));  // open: gt, lt
  Comparator #(.width(6)) comparator_6 (.a(Opcode), .b(6'b000010), .eq(comparator_6_eq));  // open: gt, lt
  assign {Jump, RegDst, ALUSrc, MemToReg, RegWrite, MemRead, MemWrite, Branch, ALUOp} = comparator_1_eq ? 10'h1aa : 10'bz;  // Controlled_Buffer controlled_buffer_1
  assign {Jump, RegDst, ALUSrc, MemToReg, RegWrite, MemRead, MemWrite, Branch, ALUOp} = comparator_2_eq ? 10'hc0 : 10'bz;  // Controlled_Buffer controlled_buffer_2
  assign {Jump, RegDst, ALUSrc, MemToReg, RegWrite, MemRead, MemWrite, Branch, ALUOp} = comparator_3_eq ? 10'hf0 : 10'bz;  // Controlled_Buffer controlled_buffer_3
  assign {Jump, RegDst, ALUSrc, MemToReg, RegWrite, MemRead, MemWrite, Branch, ALUOp} = comparator_4_eq ? 10'h88 : 10'bz;  // Controlled_Buffer controlled_buffer_4
  assign {Jump, RegDst, ALUSrc, MemToReg, RegWrite, MemRead, MemWrite, Branch, ALUOp} = comparator_5_eq ? 10'h5 : 10'bz;  // Controlled_Buffer controlled_buffer_5
  assign {Jump, RegDst, ALUSrc, MemToReg, RegWrite, MemRead, MemWrite, Branch, ALUOp} = comparator_6_eq ? 10'h200 : 10'bz;  // Controlled_Buffer controlled_buffer_6

  // Notes on the sheet:
  //   R-Type
  //   Addi
  //   Load
  //   Store
  //   Branch
  //   Jump
endmodule

module Debug_Circuit (
  input  [5:0] Funct,
  input  [5:0] Opcode,
  input  [25:0] Inst,
  output [5:0] inst3,
  output [5:0] inst2,
  output [5:0] inst1,
  output [5:0] inst0,
  output [5:0] out_8,
  output [5:0] out_9,
  output [5:0] out_10,
  output [5:0] out_11,
  output [5:0] out_12,
  output [5:0] out_13,
  output [5:0] out_14,
  output [5:0] out_15,
  output [5:0] out_16,
  output [5:0] out_17,
  output [5:0] out_18,
  output [5:0] out_19
);

  wire and_1_out, comparator_1_eq, not_1_out;
  wire [9:0] func_parser_1_add;
  wire [25:0] controlled_buffer_1_out;
  wire [31:6] controlled_buffer_2_out;

  Comparator #(.width(6)) comparator_1 (.a({6{1'b0}}), .b(Opcode), .eq(comparator_1_eq));  // open: gt, lt
  not not_1 (not_1_out, comparator_1_eq);
  assign controlled_buffer_1_out = comparator_1_eq ? Inst : 26'bz;  // Controlled_Buffer controlled_buffer_1
  func_parser func_parser_1 (
    .in_1(Funct), .Enable(comparator_1_eq), .add(func_parser_1_add[0]), .subs(func_parser_1_add[1]),
    .\and (func_parser_1_add[2]), .\or (func_parser_1_add[3]), .less_than(func_parser_1_add[4]));
  opcode_parser opcode_parser_1 (
    .in_1(Opcode), .Enable(not_1_out), .addi(func_parser_1_add[5]), .load(func_parser_1_add[6]),
    .store(func_parser_1_add[7]), .branch(func_parser_1_add[8]), .jump(func_parser_1_add[9]));
  assign {controlled_buffer_2_out[31:30], inst0, controlled_buffer_2_out[23:22], inst1, controlled_buffer_2_out[15:14], inst2, controlled_buffer_2_out[7:6], inst3} = func_parser_1_add[5] ? 32'h1040409 : 32'bz;  // Controlled_Buffer controlled_buffer_2
  assign {controlled_buffer_2_out[31:30], inst0, controlled_buffer_2_out[23:22], inst1, controlled_buffer_2_out[15:14], inst2, controlled_buffer_2_out[7:6], inst3} = func_parser_1_add[6] ? 32'hc170000 : 32'bz;  // Controlled_Buffer controlled_buffer_3
  assign {controlled_buffer_2_out[31:30], inst0, controlled_buffer_2_out[23:22], inst1, controlled_buffer_2_out[15:14], inst2, controlled_buffer_2_out[7:6], inst3} = func_parser_1_add[7] ? 32'h13170000 : 32'bz;  // Controlled_Buffer controlled_buffer_4
  assign {controlled_buffer_2_out[31:30], inst0, controlled_buffer_2_out[23:22], inst1, controlled_buffer_2_out[15:14], inst2, controlled_buffer_2_out[7:6], inst3} = func_parser_1_add[8] ? 32'h2051100 : 32'bz;  // Controlled_Buffer controlled_buffer_5
  assign {controlled_buffer_2_out[31:30], inst0, controlled_buffer_2_out[23:22], inst1, controlled_buffer_2_out[15:14], inst2, controlled_buffer_2_out[7:6], inst3} = func_parser_1_add[9] ? 32'ha000000 : 32'bz;  // Controlled_Buffer controlled_buffer_6
  assign {controlled_buffer_2_out[31:30], inst0, controlled_buffer_2_out[23:22], inst1, controlled_buffer_2_out[15:14], inst2, controlled_buffer_2_out[7:6], inst3} = func_parser_1_add[0] ? 32'h1040400 : 32'bz;  // Controlled_Buffer controlled_buffer_7
  assign {controlled_buffer_2_out[31:30], inst0, controlled_buffer_2_out[23:22], inst1, controlled_buffer_2_out[15:14], inst2, controlled_buffer_2_out[7:6], inst3} = func_parser_1_add[1] ? 32'h13150200 : 32'bz;  // Controlled_Buffer controlled_buffer_8
  assign {controlled_buffer_2_out[31:30], inst0, controlled_buffer_2_out[23:22], inst1, controlled_buffer_2_out[15:14], inst2, controlled_buffer_2_out[7:6], inst3} = func_parser_1_add[2] ? 32'h10e0400 : 32'bz;  // Controlled_Buffer controlled_buffer_9
  assign {controlled_buffer_2_out[31:30], inst0, controlled_buffer_2_out[23:22], inst1, controlled_buffer_2_out[15:14], inst2, controlled_buffer_2_out[7:6], inst3} = func_parser_1_add[3] ? 32'hf120000 : 32'bz;  // Controlled_Buffer controlled_buffer_10
  assign {controlled_buffer_2_out[31:30], inst0, controlled_buffer_2_out[23:22], inst1, controlled_buffer_2_out[15:14], inst2, controlled_buffer_2_out[7:6], inst3} = func_parser_1_add[4] ? 32'h130c1400 : 32'bz;  // Controlled_Buffer controlled_buffer_11
  and and_1 (and_1_out, ~func_parser_1_add[0], ~func_parser_1_add[1], ~func_parser_1_add[2], ~func_parser_1_add[3], ~func_parser_1_add[4], ~func_parser_1_add[5], ~func_parser_1_add[6], ~func_parser_1_add[7], ~func_parser_1_add[8], ~func_parser_1_add[9]);  // AND_Gate
  assign {controlled_buffer_2_out[31:30], inst0, controlled_buffer_2_out[23:22], inst1, controlled_buffer_2_out[15:14], inst2, controlled_buffer_2_out[7:6], inst3} = and_1_out ? 32'he0f1000 : 32'bz;  // Controlled_Buffer controlled_buffer_12
  Register_parser register_parser_1 (.\reg (controlled_buffer_1_out[25:21]), .ch2(out_10), .ch1(out_9), .ch0(out_8));
  Register_parser register_parser_2 (.\reg (controlled_buffer_1_out[20:16]));  // open: ch2, ch1, ch0
  Register_parser register_parser_3 (.\reg (controlled_buffer_1_out[15:11]));  // open: ch2, ch1, ch0
endmodule

module func_parser (
  input  [5:0] in_1,
  input  Enable,
  output add,
  output subs,
  output \and ,
  output \or ,
  output less_than
);

  wire and_1_out, and_2_out, and_3_out, and_4_out, and_5_out, not_1_out, not_2_out, not_3_out, not_4_out,
       not_5_out, not_6_out, not_7_out, not_8_out, not_9_out, not_10_out, not_11_out, not_12_out, not_13_out,
       not_14_out, not_15_out, not_16_out, not_17_out, not_18_out, not_19_out;

  not not_1 (not_1_out, in_1[4]);
  not not_2 (not_2_out, in_1[3]);
  not not_3 (not_3_out, in_1[2]);
  not not_4 (not_4_out, in_1[1]);
  not not_5 (not_5_out, in_1[0]);
  not not_6 (not_6_out, in_1[4]);
  not not_7 (not_7_out, in_1[3]);
  not not_8 (not_8_out, in_1[2]);
  not not_9 (not_9_out, in_1[0]);
  not not_10 (not_10_out, in_1[4]);
  not not_11 (not_11_out, in_1[3]);
  not not_12 (not_12_out, in_1[1]);
  not not_13 (not_13_out, in_1[0]);
  not not_14 (not_14_out, in_1[4]);
  not not_15 (not_15_out, in_1[3]);
  not not_16 (not_16_out, in_1[1]);
  not not_17 (not_17_out, in_1[4]);
  not not_18 (not_18_out, in_1[2]);
  not not_19 (not_19_out, in_1[0]);
  and and_1 (and_1_out, in_1[5], not_1_out, not_2_out, not_3_out, not_4_out, not_5_out);
  and and_2 (and_2_out, in_1[5], not_6_out, not_7_out, not_8_out, in_1[1], not_9_out);
  and and_3 (and_3_out, in_1[5], not_10_out, not_11_out, in_1[2], not_12_out, not_13_out);
  and and_4 (and_4_out, in_1[5], not_14_out, not_15_out, in_1[2], not_16_out, in_1[0]);
  and and_5 (and_5_out, in_1[5], not_17_out, in_1[3], not_18_out, in_1[1], not_19_out);
  and and_6 (add, and_1_out, Enable);
  and and_7 (subs, and_2_out, Enable);
  and and_8 (\and , and_3_out, Enable);
  and and_9 (\or , and_4_out, Enable);
  and and_10 (less_than, and_5_out, Enable);
endmodule

module opcode_parser (
  input  [5:0] in_1,
  input  Enable,
  output addi,
  output load,
  output store,
  output branch,
  output jump
);

  wire and_1_out, and_2_out, and_3_out, and_4_out, and_5_out, not_1_out, not_2_out, not_3_out, not_4_out,
       not_5_out, not_6_out, not_7_out, not_8_out, not_9_out, not_10_out, not_11_out, not_12_out, not_13_out,
       not_14_out, not_15_out, not_16_out, not_17_out, not_18_out, not_19_out, not_20_out;

  not not_1 (not_1_out, in_1[5]);
  not not_2 (not_2_out, in_1[4]);
  not not_3 (not_3_out, in_1[2]);
  not not_4 (not_4_out, in_1[1]);
  not not_5 (not_5_out, in_1[0]);
  not not_6 (not_6_out, in_1[4]);
  not not_7 (not_7_out, in_1[3]);
  not not_8 (not_8_out, in_1[2]);
  not not_9 (not_9_out, in_1[4]);
  not not_10 (not_10_out, in_1[2]);
  not not_11 (not_11_out, in_1[5]);
  not not_12 (not_12_out, in_1[4]);
  not not_13 (not_13_out, in_1[3]);
  not not_14 (not_14_out, in_1[1]);
  not not_15 (not_15_out, in_1[0]);
  not not_16 (not_16_out, in_1[5]);
  not not_17 (not_17_out, in_1[4]);
  not not_18 (not_18_out, in_1[3]);
  not not_19 (not_19_out, in_1[2]);
  not not_20 (not_20_out, in_1[0]);
  and and_1 (and_1_out, not_1_out, not_2_out, in_1[3], not_3_out, not_4_out, not_5_out);
  and and_2 (and_2_out, in_1[5], not_6_out, not_7_out, not_8_out, in_1[1], in_1[0]);
  and and_3 (and_3_out, in_1[5], not_9_out, in_1[3], not_10_out, in_1[1], in_1[0]);
  and and_4 (and_4_out, not_11_out, not_12_out, not_13_out, in_1[2], not_14_out, not_15_out);
  and and_5 (and_5_out, not_16_out, not_17_out, not_18_out, not_19_out, in_1[1], not_20_out);
  and and_6 (addi, and_1_out, Enable);
  and and_7 (load, and_2_out, Enable);
  and and_8 (store, and_3_out, Enable);
  buf and_9 (branch, and_4_out);  // AND_Gate
  and and_10 (jump, and_5_out, Enable);
endmodule

module Display_Driver (
  input  [5:0] in_1,
  output [6:0] col0,
  output [6:0] col1,
  output [6:0] col2,
  output [6:0] col3,
  output [6:0] col4
);

  wire [3:0] undriven_2;
  wire [4:0] undriven;
  wire [6:0] multiplexer_1_out, multiplexer_2_out, multiplexer_3_out, multiplexer_4_out, multiplexer_5_out,
       multiplexer_6_out, multiplexer_7_out, multiplexer_8_out, multiplexer_9_out, multiplexer_10_out;
  wire [15:7] rom_2_data;
  wire [19:3] rom_1_data;

  Multiplexer #(.select(5), .width(7)) multiplexer_1 (
    .in0({7{1'b0}}), .in1(7'b0111111), .in2({7{1'b1}}), .in3(7'b0111110), .in4({7{1'b1}}), .in5({7{1'b1}}),
    .in6({7{1'b1}}), .in7(7'b0111110), .in8({7{1'b1}}), .in9(7'b1000001), .in10(7'b1000110),
    .in11({7{1'b1}}), .in12({7{1'b1}}), .in13({7{1'b1}}), .in14({7{1'b1}}), .in15(7'b0111110),
    .in16({7{1'b1}}), .in17(7'b0111110), .in18({7{1'b1}}), .in19(7'b0110001), .in20(7'b1000000),
    .in21(7'b1111110), .in22(7'b1111100), .in23({7{1'b1}}), .in24(7'b1100011), .in25(7'b1110000),
    .in26(7'b1000011), .in27({7{1'b0}}), .in28(7'b0100111), .in29(7'b0100010), .in30(7'b1111000),
    .in31(7'b1111001), .out(multiplexer_1_out), .sel(undriven));  // open: en
  Multiplexer #(.select(5), .width(7)) multiplexer_2 (
    .in0({7{1'b0}}), .in1(7'b1000100), .in2(7'b1001001), .in3(7'b1000001), .in4(7'b1000001),
    .in5(7'b1001001), .in6(7'b1001000), .in7(7'b1000001), .in8(7'b0001000), .in9(7'b1000001),
    .in10(7'b1000001), .in11(7'b0001000), .in12(7'b0000001), .in13(7'b0100000), .in14(7'b0100000),
    .in15(7'b1000001), .in16(7'b1001000), .in17(7'b1000001), .in18(7'b1000100), .in19(7'b1001001),
    .in20(7'b1000000), .in21(7'b0000001), .in22(7'b0000010), .in23(7'b0000010), .in24(7'b0010100),
    .in25(7'b0001000), .in26(7'b1000101), .in27(7'b1000001), .in28(7'b1001001), .in29(7'b1000001),
    .in30(7'b0001000), .in31(7'b1001001), .out(multiplexer_2_out), .sel(undriven));  // open: en
  ROM #(.addrWidth(6), .dataWidth(20)) rom_1 (
    .addr(in_1), .data({rom_1_data[19], col0, rom_1_data[11], col1, rom_1_data[3], col2[6:4]}));  // open: sel
  ROM #(.addrWidth(6), .dataWidth(20)) rom_2 (
    .addr(in_1), .data({col2[3:0], rom_2_data[15], col3, rom_2_data[7], col4}));  // open: sel
  Multiplexer #(.select(5), .width(7)) multiplexer_3 (
    .in0({7{1'b0}}), .in1(7'b1000100), .in2(7'b1001001), .in3(7'b1000001), .in4(7'b1000001),
    .in5(7'b1001001), .in6(7'b1001000), .in7(7'b1001001), .in8(7'b0001000), .in9({7{1'b1}}),
    .in10(7'b1000001), .in11(7'b0001000), .in12(7'b0000001), .in13(7'b0011000), .in14(7'b0010000),
    .in15(7'b1000001), .in16(7'b1001000), .in17(7'b1000011), .in18(7'b1000100), .in19(7'b1001001),
    .in20({7{1'b1}}), .in21(7'b0000001), .in22(7'b0000001), .in23(7'b0001100), .in24(7'b0001000),
    .in25(7'b0000111), .in26(7'b1001001), .in27({7{1'b1}}), .in28(7'b1001001), .in29(7'b1001001),
    .in30(7'b0001000), .in31(7'b1001001), .out(multiplexer_3_out), .sel(undriven));  // open: en
  // Probe on nothing
  Multiplexer #(.select(5), .width(7)) multiplexer_4 (
    .in0({7{1'b0}}), .in1(7'b1000100), .in2(7'b1001001), .in3(7'b1000001), .in4(7'b1000001),
    .in5(7'b1001001), .in6(7'b1000000), .in7(7'b1001001), .in8(7'b0001000), .in9(7'b1000001),
    .in10(7'b1111110), .in11(7'b0010100), .in12(7'b0000001), .in13(7'b0100000), .in14(7'b0001000),
    .in15(7'b1000001), .in16(7'b1001000), .in17(7'b1000001), .in18(7'b1000100), .in19(7'b1001001),
    .in20(7'b1000000), .in21(7'b0000001), .in22(7'b0000010), .in23(7'b0000010), .in24(7'b0010100),
    .in25(7'b0001000), .in26(7'b1010001), .in27(7'b0000001), .in28(7'b1001001), .in29(7'b1001001),
    .in30({7{1'b1}}), .in31(7'b1001001), .out(multiplexer_4_out), .sel(undriven));  // open: en
  Multiplexer #(.select(5), .width(7)) multiplexer_5 (
    .in0({7{1'b0}}), .in1(7'b0111111), .in2(7'b0110110), .in3(7'b0100010), .in4(7'b0111110),
    .in5(7'b1001001), .in6(7'b1000000), .in7(7'b0101110), .in8({7{1'b1}}), .in9(7'b1000001),
    .in10(7'b1000000), .in11(7'b1100011), .in12(7'b0000001), .in13({7{1'b1}}), .in14({7{1'b1}}),
    .in15(7'b0111110), .in16(7'b0110000), .in17(7'b0111110), .in18(7'b0111011), .in19(7'b1000110),
    .in20(7'b1000000), .in21(7'b1111110), .in22(7'b1111100), .in23({7{1'b1}}), .in24(7'b1100011),
    .in25(7'b1110000), .in26(7'b1100001), .in27({7{1'b0}}), .in28(7'b0110001), .in29(7'b0110110),
    .in30(7'b0001000), .in31(7'b1000110), .out(multiplexer_5_out), .sel(undriven));  // open: en
  Multiplexer #(.select(4), .width(7)) multiplexer_6 (
    .in0(7'b0111110), .in1({7{1'b0}}), .in2(7'b0100111), .in3(7'b0100010), .in4(7'b1111000),
    .in5(7'b1111001), .in6(7'b0111110), .in7(7'b1000000), .in8(7'b0110110), .in9(7'b0110010),
    .in10(7'b0010010), .in11({7{1'b0}}), .in12({7{1'b0}}), .in13({7{1'b0}}), .in14({7{1'b0}}),
    .in15({7{1'b0}}), .out(multiplexer_6_out), .sel(undriven_2));  // open: en
  Multiplexer #(.select(4), .width(7)) multiplexer_7 (
    .in0(7'b1000101), .in1(7'b1000001), .in2(7'b1001001), .in3(7'b1000001), .in4(7'b0001000),
    .in5(7'b1001001), .in6(7'b1001001), .in7(7'b1000111), .in8(7'b1001001), .in9(7'b1001001),
    .in10(7'b0101010), .in11(7'b0000101), .in12({7{1'b0}}), .in13({7{1'b0}}), .in14({7{1'b0}}),
    .in15({7{1'b0}}), .out(multiplexer_7_out), .sel(undriven_2));  // open: en
  Multiplexer #(.select(4), .width(7)) multiplexer_8 (
    .in0(7'b1001001), .in1({7{1'b1}}), .in2(7'b1001001), .in3(7'b1001001), .in4(7'b0001000),
    .in5(7'b1001001), .in6(7'b1001001), .in7(7'b1001000), .in8(7'b1001001), .in9(7'b1001001),
    .in10({7{1'b1}}), .in11(7'b0000110), .in12({7{1'b0}}), .in13({7{1'b0}}), .in14({7{1'b0}}),
    .in15({7{1'b0}}), .out(multiplexer_8_out), .sel(undriven_2));  // open: en
  Multiplexer #(.select(4), .width(7)) multiplexer_9 (
    .in0(7'b1010001), .in1(7'b0000001), .in2(7'b1001001), .in3(7'b1001001), .in4({7{1'b1}}),
    .in5(7'b1001001), .in6(7'b1001001), .in7(7'b1001000), .in8(7'b1001001), .in9(7'b1001001),
    .in10(7'b0101010), .in11({7{1'b0}}), .in12({7{1'b0}}), .in13({7{1'b0}}), .in14({7{1'b0}}),
    .in15({7{1'b0}}), .out(multiplexer_9_out), .sel(undriven_2));  // open: en
  Multiplexer #(.select(4), .width(7)) multiplexer_10 (
    .in0(7'b0111110), .in1({7{1'b0}}), .in2(7'b0110001), .in3(7'b0110110), .in4(7'b0001000),
    .in5(7'b1000110), .in6(7'b0000110), .in7(7'b1110000), .in8(7'b0110110), .in9(7'b0111110),
    .in10(7'b0100100), .in11({7{1'b0}}), .in12({7{1'b0}}), .in13({7{1'b0}}), .in14({7{1'b0}}),
    .in15({7{1'b0}}), .out(multiplexer_10_out), .sel(undriven_2));  // open: en

  // Notes on the sheet:
  //   contents of rom_1 (hex, n*v repeats v):
  //   0 3f444 7f494 3e414 7f414 7f494 7f484 3e414 7f080 41417 46414 7f080 7f010 7f201 7f201 3e414 7f484
  //   3e414 7f444 31494 40407 7e010 7c020 7f020 63140 70080 43454 3e454 417 27494 22414 78080 79494 3e494
  //   40474 36494 32494 122a7 50
  //   contents of rom_2 (hex, n*v repeats v):
  //   0 4443f 94936 14122 1413e 94949 84040 9492e 8087f f4141 17e40 81463 10101 8207f 87f 1413e 84830
  //   3413e 4443b 94946 f4040 1017e 1027c c027f 81463 70870 95161 9513e f0100 94931 94936 87f08 94946
  //   94906 84870 94936 9493e f2a24 60000
endmodule

module ALU_Control (
  input  [1:0] ALUOp,
  input  [5:0] Funct,
  output [3:0] Operation
);

  wire and_1_out, comparator_2_eq, comparator_3_eq, comparator_4_eq, comparator_5_eq;
  wire [3:0] bit_extender_1_out;

  Bit_Extender #(.in_width(6), .out_width(4)) bit_extender_1 (.in(Funct), .out(bit_extender_1_out));
  and and_1 (and_1_out, ~ALUOp[0], ~ALUOp[1]);  // AND_Gate
  Comparator #(.width(4)) comparator_1 (.a(bit_extender_1_out), .b(4'b0000), .eq(and_1_out));  // open: gt, lt
  Comparator #(.width(4)) comparator_2 (.a(bit_extender_1_out), .b(4'b0010), .eq(comparator_2_eq));  // open: gt, lt
  Comparator #(.width(4)) comparator_3 (.a(bit_extender_1_out), .b(4'b0100), .eq(comparator_3_eq));  // open: gt, lt
  Comparator #(.width(4)) comparator_4 (.a(bit_extender_1_out), .b(4'b0101), .eq(comparator_4_eq));  // open: gt, lt
  Comparator #(.width(4)) comparator_5 (.a(bit_extender_1_out), .b(4'b1010), .eq(comparator_5_eq));  // open: gt, lt
  and and_2 (comparator_2_eq, ~and_1_out, ALUOp[0]);  // AND_Gate
  assign Operation = and_1_out ? 4'b0010 : 4'bz;  // Controlled_Buffer controlled_buffer_1
  assign Operation = comparator_2_eq ? 4'b0110 : 4'bz;  // Controlled_Buffer controlled_buffer_2
  assign Operation = comparator_3_eq ? 4'b0000 : 4'bz;  // Controlled_Buffer controlled_buffer_3
  assign Operation = comparator_4_eq ? 4'b0001 : 4'bz;  // Controlled_Buffer controlled_buffer_4
  assign Operation = comparator_5_eq ? 4'b0111 : 4'bz;  // Controlled_Buffer controlled_buffer_5

  // Notes on the sheet:
  //   Suma
  //   Resta
  //   And
  //   Or
  //   Less Than
endmodule

module Register_parser (
  input  [4:0] \reg ,
  output [5:0] ch2,
  output [5:0] ch1,
  output [5:0] ch0
);

  wire [15:6] multiplexer_1_out;

  Multiplexer #(.select(5), .width(16)) multiplexer_1 (
    .in0(16'h1a12), .in1(16'h114), .in2(16'h161b), .in3(16'h161c), .in4(16'h11b), .in5(16'h11c),
    .in6(16'h11d), .in7(16'h11e), .in8(16'h141b), .in9(16'h141c), .in10(16'h141d), .in11(16'h141e),
    .in12(16'h141f), .in13(16'h1420), .in14(16'h1421), .in15(16'h1422), .in16(16'h131b), .in17(16'h131c),
    .in18(16'h131d), .in19(16'h131e), .in20(16'h131f), .in21(16'h1320), .in22(16'h1321), .in23(16'h1322),
    .in24(16'h1423), .in25(16'h1424), .in26(16'hb1b), .in27(16'hb1c), .in28(16'h710), .in29(16'h1310),
    .in30(16'h610), .in31(16'h1201), .out({multiplexer_1_out[15:14], ch1, multiplexer_1_out[7:6], ch2}),
    .sel(\reg ));  // open: en

  assign ch0 = 6'b100101;
endmodule
